# Fritzing sketch Mega2560_esp32S3 (saved by Fritzing 0.9.8b)
breadboards: 1

parts:
  LED = LED - 5mm [color="Red (633nm)" current=0.030 package="5 mm [THT]"]
  S1 = Pushbutton [package=THT]
  Q1 = NPN-Transistor [part_number="CS 9013" package="TO92 [THT]"]
  U1 = RELAY [part_number=Relay package=relay-t9a-2]
  S2 = Pushbutton [package=THT]
  R2 = Resistor [tolerance=±5% power=0.25 resistance=680 package=THT]
  S4 = Pushbutton [package=THT]
  S3 = Pushbutton [package=THT]
  S5 = Pushbutton [package=THT]
  S7 = Pushbutton [package=THT]
  S8 = Pushbutton [package=THT]
  S6 = Pushbutton [package=THT]
  S10 = Pushbutton [package=THT]
  S9 = Pushbutton [package=THT]
  Mod1 = Heltec WiFi LoRa 32 V2 [part_number="ESP32 S3"]
  IC1 = Voltage Regulator [part_number=7805 package=to-220-alt]
  VCC1 = Battery block 9V [part_number=24V]
  R21 = Resistor [tolerance=±5% power=0.25 resistance=100k package=THT]
  D1 = Rectifier Diode [part_number=1N4001 package="300 mil [THT]"]
  C1 = Electrolytic Capacitor [capacitance=10µF voltage=35V package="100 mil [THT, electrolytic]"]
  C2 = Electrolytic Capacitor [capacitance=10µF voltage=35V package="100 mil [THT, electrolytic]"]
  L2 = Inductor [package="400 mil [THT]"]
  LED1 = LED - 5mm [color="Red (633nm)" current=0.030 package="5 mm [THT]"]  # not connected
  R22 = Resistor [tolerance=±5% power=0.25 resistance=680 package=THT]
  LED2 = LED - 5mm [color="Red (633nm)" current=0.030 package="5 mm [THT]"]  # not connected
  LED3 = LED - 5mm [color="Red (633nm)" current=0.030 package="5 mm [THT]"]  # not connected
  R23 = Resistor [tolerance=±5% power=0.25 resistance=680 package=THT]
  R24 = Resistor [tolerance=±5% power=0.25 resistance=680 package=THT]
  LED4 = LED - 5mm [color="Red (633nm)" current=0.030 package="5 mm [THT]"]  # not connected
  LED5 = LED - 5mm [color="Red (633nm)" current=0.030 package="5 mm [THT]"]  # not connected
  R25 = Resistor [tolerance=±5% power=0.25 resistance=680 package=THT]
  R26 = Resistor [tolerance=±5% power=0.25 resistance=680 package=THT]
  LED6 = LED - 5mm [color="Red (633nm)" current=0.030 package="5 mm [THT]"]
  LED7 = LED - 5mm [color="Red (633nm)" current=0.030 package="5 mm [THT]"]  # not connected
  LED8 = LED - 5mm [color="Red (633nm)" current=0.030 package="5 mm [THT]"]  # not connected
  LED9 = LED - 5mm [color="Red (633nm)" current=0.030 package="5 mm [THT]"]  # not connected
  R27 = Resistor [tolerance=±5% power=0.25 resistance=680 package=THT]
  R28 = Resistor [tolerance=±5% power=0.25 resistance=680 package=THT]
  R29 = Resistor [tolerance=±5% power=0.25 resistance=680 package=THT]
  R30 = Resistor [tolerance=±5% power=0.25 resistance=680 package=THT]
  S20 = Pushbutton [package=THT]
  S18 = Pushbutton [package=THT]
  S19 = Pushbutton [package=THT]
  S17 = Pushbutton [package=THT]
  S11 = Pushbutton [package=THT]
  S16 = Pushbutton [package=THT]
  S14 = Pushbutton [package=THT]
  S13 = Pushbutton [package=THT]
  S15 = Pushbutton [package=THT]
  S12 = Pushbutton [package=THT]
  LED10 = LED - 5mm [color="Red (633nm)" current=0.030 package="5 mm [THT]"]
  LED11 = LED - 5mm [color="Red (633nm)" current=0.030 package="5 mm [THT]"]  # not connected
  LED12 = LED - 5mm [color="Red (633nm)" current=0.030 package="5 mm [THT]"]  # not connected
  LED13 = LED - 5mm [color="Red (633nm)" current=0.030 package="5 mm [THT]"]  # not connected
  LED14 = LED - 5mm [color="Red (633nm)" current=0.030 package="5 mm [THT]"]  # not connected
  LED15 = LED - 5mm [color="Red (633nm)" current=0.030 package="5 mm [THT]"]  # not connected
  LED16 = LED - 5mm [color="Red (633nm)" current=0.030 package="5 mm [THT]"]  # not connected
  LED17 = LED - 5mm [color="Red (633nm)" current=0.030 package="5 mm [THT]"]  # not connected
  LED18 = LED - 5mm [color="Red (633nm)" current=0.030 package="5 mm [THT]"]  # not connected
  LED19 = LED - 5mm [color="Red (633nm)" current=0.030 package="5 mm [THT]"]
  R31 = Resistor [tolerance=±5% power=0.25 resistance=680 package=THT]
  R32 = Resistor [tolerance=±5% power=0.25 resistance=680 package=THT]
  R33 = Resistor [tolerance=±5% power=0.25 resistance=680 package=THT]
  R34 = Resistor [tolerance=±5% power=0.25 resistance=680 package=THT]
  R35 = Resistor [tolerance=±5% power=0.25 resistance=680 package=THT]
  R36 = Resistor [tolerance=±5% power=0.25 resistance=680 package=THT]
  R37 = Resistor [tolerance=±5% power=0.25 resistance=680 package=THT]
  R38 = Resistor [tolerance=±5% power=0.25 resistance=680 package=THT]
  R39 = Resistor [tolerance=±5% power=0.25 resistance=680 package=THT]
  R40 = Resistor [tolerance=±5% power=0.25 resistance=680 package=THT]
  RFID = ID-12_20 [package=id-12_smd]
  OLED = WeMos D1 Mini Relay Shield
  R41 = Resistor [tolerance=±5% power=0.25 resistance=220 part_number=2KΩ package=THT]
  R42 = Resistor [tolerance=±5% power=0.25 resistance=220 part_number=3.3KΩ package=THT]
  R43 = Resistor [tolerance=±5% power=0.25 resistance=220 part_number=2KΩ package=THT]
  R44 = Resistor [tolerance=±5% power=0.25 resistance=220 part_number=3.3KΩ package=THT]
  Mod2 = Heltec WiFi LoRa 32 V2 [part_number=ESP32]
  MEGA_2560 = Arduino Mega 2560 (Rev3)
  D2 = P1000K [part_number=P1000K]

nets:
  N1: LED.anode, Mod1.pin_35, IC1.OUT, C2.+, LED6.anode, LED10.anode, LED19.anode
  2: S1.leg0, R2.Pin_1
  GND: S1.leg1, Q1.E, U1.NO, S2.leg1, S4.leg1, S5.leg1, S7.leg1, S8.leg1, S6.leg1, S9.leg1, Mod1.pin_36, IC1.GND, VCC1.-, C1.-, C2.-, S20.leg1, S18.leg1, S19.leg1, S17.leg1, S11.leg1, S16.leg1, S14.leg1, S13.leg1, S15.leg1, S12.leg1, RFID.FUTURE, OLED.G, R42.Pin_1, R44.Pin_1, Mod2.GND, MEGA_2560.GND
  N2: Q1.B, R21.Pin_0
  N3: Q1.C, U1.COIL2, D1.anode
  5V: U1.COIL1, D1.cathode, Mod2.pin_20, MEGA_2560.5V
  N4: U1.MAIN, L2.pin_0, D2.anode
  3: S2.leg0, R22.Pin_1
  5: S4.leg0, R24.Pin_1
  4: S3.leg0, R23.Pin_1
  6: S5.leg0, R25.Pin_1
  8: S7.leg0, R27.Pin_1
  9: S8.leg0, R28.Pin_1
  7: S6.leg0, R26.Pin_1
  11: S10.leg0, R30.Pin_1
  10: S9.leg0, R29.Pin_1
  N5: IC1.IN, VCC1.+, C1.+, L2.pin_1, D2.cathode
  net label: R21.Pin_1
  40: S20.leg0, R33.Pin_1
  38: S18.leg0, R34.Pin_1
  39: S19.leg0, R37.Pin_1
  21: S17.leg0, R40.Pin_1
  15: S11.leg0, R31.Pin_1
  20: S16.leg0, R35.Pin_1, OLED.A0, OLED.RST
  18: S14.leg0, R36.Pin_1, R41.Pin_0
  17: S13.leg0, R38.Pin_1, R43.Pin_1, R44.Pin_0
  19: S15.leg0, R32.Pin_1, R43.Pin_0
  16: S12.leg0, R39.Pin_1, R41.Pin_1, R42.Pin_0
  3.3V: OLED.TX

notes:
  電磁閥
